# Fritzing sketch schematic diagram (saved by Fritzing 0.9.3b)

parts:
  MH-ET_LIVE_ESP32_DEVKIT1 = MH-ET LIVE ESP32 DEVKIT 38 pins
  HC-SR04_Sensor_1 = HC-SR04 Ultrasonic Distance Sensor
  J1 = Basic Servo
  A1 = DHT22 module
  Part1 = HC-SR501 Body Sensor Module
  ZS-042_RTC1 = ZS-042 RTC Module

nets:
  N1: MH-ET_LIVE_ESP32_DEVKIT1.IO27, Part1.OUT
  N2: MH-ET_LIVE_ESP32_DEVKIT1.IO14, HC-SR04_Sensor_1.TRIG, HC-SR04_Sensor_1.ECHO
  GND: MH-ET_LIVE_ESP32_DEVKIT1.GND, HC-SR04_Sensor_1.GND, J1.gnd, A1.-, Part1.GND, ZS-042_RTC1.GND
  N3: MH-ET_LIVE_ESP32_DEVKIT1.IO13, A1.Out
  VCC: MH-ET_LIVE_ESP32_DEVKIT1.5V, HC-SR04_Sensor_1.VCC, J1.vcc, A1.+, Part1.VCC, ZS-042_RTC1.VCC
  N4: MH-ET_LIVE_ESP32_DEVKIT1.IO22, ZS-042_RTC1.SCL
  N5: MH-ET_LIVE_ESP32_DEVKIT1.IO21, ZS-042_RTC1.SDA
  N6: MH-ET_LIVE_ESP32_DEVKIT1.IO18, J1.pulse

custom parts:
  MH-ET LIVE ESP32 DEVKIT 38 pins: http://mh.nodebb.com/topic/2/mh-et-live-esp32-devkit
  DHT22 module: DHT22 module. Pins VCC Data GND.
  HC-SR501 Body Sensor Module: Pyroelectric Infrared PIR Motion Sensor Detector Module
